# Fritzing sketch laserstat_emulator (saved by Fritzing 0.8.7b)
breadboards: 1

parts:
  S1 = Pushbutton [package="[THT]"]
  S2 = Pushbutton [package="[THT]"]
  S3 = Pushbutton [package="[THT]"]
  S4 = Pushbutton [package="[THT]"]
  R1 = Resistor [tolerance=±5% resistance=220 package=THT]
  R2 = Resistor [tolerance=±5% resistance=220 package=THT]
  R3 = Resistor [tolerance=±5% resistance=220 package=THT]
  R4 = Resistor [tolerance=±5% resistance=220 package=THT]

nets:
  N1: S1.Pin_1, S1.Pin_2, R1.Pin_0
  N2: S1.Pin_3, S1.Pin_4, S2.Pin_3, S2.Pin_4, S3.Pin_3, S3.Pin_4, S4.Pin_3, S4.Pin_4
  N3: S2.Pin_1, S2.Pin_2, R3.Pin_0
  N4: S3.Pin_1, S3.Pin_2, R4.Pin_0
  N5: S4.Pin_1, S4.Pin_2, R2.Pin_0
  N6: R1.Pin_1, R2.Pin_1, R3.Pin_1, R4.Pin_1
